# Fritzing sketch wiring-diagram (saved by Fritzing 0.9.4)

parts:
  A1 = ESP32 devkit 38p expansion board
  U1 = ESP32-38PinWide [part_number=ESP32-38PinWide]  # not connected
  A2 = GY-BMP280 Breakout
  USBTTL1 = Micro USB B Plug
  M1 = INA219 DC Current Monitor Module [part_number=CJMCU]
  MOD1 = MT3608 Boost No usb
  Part1 = Solar Cell
  Bat1 = battery_holder_single_18650
  Mod1 = tp5000 [package=THT]
  D1 = Rectifier Diode [package="Melf DO-213 AA [SMD]"]  # not connected
  S1 = Round Pushbutton

nets:
  N1: A1.Pin_17, A1.Pin_57, M1.VCC
  N2: A1.Pin_50, A1.Pin_51, A1.Pin_52, A1.Pin_144, A2.Pin_2, A2.Pin_6, M1.GND
  N3: A1.Pin_58, A1.Pin_59, A1.Pin_99, A1.Pin_100, A1.Pin_157, A2.Pin_1, A2.Pin_5
  N4: A1.Pin_174, A2.Pin_4, M1.SDA
  N5: A1.Pin_177, A2.Pin_3, M1.SCL
  N6: USBTTL1.usb, MOD1.IN_(-), MOD1.OUT_(+), MOD1.OUT_(-), Part1.-, Bat1.+#0, Mod1.-IN, Mod1.-BAT
  N7: M1.Vin+, S1.leg0
  N8: M1.Vin-, MOD1.IN_(+)
  N9: Bat1.+#1, Mod1.+BAT, S1.leg1

notes:
  TP5000
  INA219
  BME280
  Lifepo4
  solar cell 6v -7v
  DC step UP MT3608
  1N5819

custom parts:
  ESP32 devkit 38p expansion board: Upgraded ESP32 38P Development ESP32-DevKitC-32 ESP-WROOM-32 Expansion Board.
  ESP32-38PinWide: Generic 38-Pin ESP32 with wide format (only access to one side of pins on a breadboard) based on Stephen Lilley's HiLetgo ESP-WROOM-32 ESP32 ESP-32S Development Board.
  INA219 DC Current Monitor Module: INA219 DC Current Monitor Module Links: INA219 product information
  MT3608 Boost No usb: Chip- MT3608 / B6289 DC to DC step up, power booster module. With adjustable output voltage. Current- 2A . || Input voltage- 2V-24V || Output voltage- 5V-28V Input interface- Inversed polarity- NO. || Led indicator- No.
  battery_holder_single_18650: single 18650 battery holder
  tp5000: Tp5000 battery charger module. Generic ebay type.
